# Fritzing sketch schemats (saved by Fritzing 0.9.10b)

parts:
  U1 = LuaNode32 / ESP32
  HC-SR04_Sensor_1 = HC-SR04 Ultrasonic Distance Sensor
  KY-1 = Keyes Relay [package=THT]
  LED1 = smd LED [color="Red (633nm)" package="0603 [SMD]"]

nets:
  N1: U1.D13, KY-1.power
  GND: U1.GND, HC-SR04_Sensor_1.GND, KY-1.ground, LED1.cathode
  3V3: U1.3V3, HC-SR04_Sensor_1.VCC, KY-1.signal
  N2: U1.D2, HC-SR04_Sensor_1.TRIG
  N3: U1.D4, HC-SR04_Sensor_1.ECHO
  N4: KY-1.NC, LED1.anode

notes:
  Tutaj napięcie wejściowe które uruchomi ten mechanizm
  Trzeba sobie zobaczyć które wyjście będzie poprawne.
  Ja dałem przykładowe wyjscie

custom parts:
  LuaNode32 / ESP32: ESP32 based LuaNode32
  Keyes Relay: The Keyes 5V relay module is suitable for SCM development, home appliance control. It uses a 5V~12V TIL control signal which can control DC / AC signal.
